// Logisim project DDNF.circ as structural Verilog: 1 circuit, main circuit main
module main (
  input  X3,
  input  X2,
  input  X1,
  output y
);

  wire nand_1_out, nand_2_out, nand_3_out, not_1_out, not_2_out, not_3_out;

  not not_1 (not_1_out, X3);
  not not_2 (not_2_out, X2);
  not not_3 (not_3_out, X1);
  nand nand_1 (nand_1_out, not_1_out, not_2_out, not_3_out);
  nand nand_2 (nand_2_out, not_1_out, X1, X2);
  nand nand_3 (nand_3_out, not_2_out, X1, X3);
  nand nand_4 (y, nand_1_out, nand_2_out, nand_3_out);
endmodule
